// Logisim project Lab 4 work.circ as structural Verilog: 4 circuits, main circuit main
module main (
  input  W,
  input  X,
  input  Y,
  input  Z,
  output A,
  output B,
  output C,
  output D
);

  wire n1_input_not_1_out_11, n1_input_not_1_out_12, n3_input_and_1_out_10, n3_input_and_1_out_11,
       n3_input_and_2_out_10, n3_input_and_2_out_11, n3_input_and_3_out_10, n3_input_and_3_out_11,
       n3_input_and_3_out_12;

  _3_Input_AND_Gate u_3_input_and_1 (
    .in_1(Z), .in_2(X), .in_3(X), .in_4(Y), .in_5(Y), .in_6(X), .out_10(n3_input_and_1_out_10),
    .out_11(n3_input_and_1_out_11));  // open: in_7, in_8, in_9, out_12
  _1_Input_NOT_Gate u_1_input_not_1 (
    .in_4(Z), .in_5(Y), .in_6(X), .out_10(D), .out_11(n1_input_not_1_out_11), .out_12(n1_input_not_1_out_12));  // open: in_1, in_2, in_3, out_7, out_8, out_9
  _3_Input_AND_Gate u_3_input_and_2 (
    .in_1(Z), .in_2(Y), .in_3(Y), .in_4(n1_input_not_1_out_11), .in_5(n1_input_not_1_out_11), .in_6(D),
    .out_10(n3_input_and_2_out_10), .out_11(n3_input_and_2_out_11));  // open: in_7, in_8, in_9, out_12
  _3_Input_OR_Gate u_3_input_or_1 (
    .in_7(n3_input_and_1_out_10), .in_8(n3_input_and_1_out_11), .in_9(W), .out_12(A));  // open: in_1, in_2, in_3, in_4, in_5, in_6, out_10, out_11
  _3_Input_AND_Gate u_3_input_and_3 (
    .in_1(D), .in_2(n1_input_not_1_out_11), .in_3(X), .in_4(Y), .in_5(n1_input_not_1_out_12),
    .in_6(n1_input_not_1_out_12), .in_7(Z), .in_8(Z), .in_9(n1_input_not_1_out_12),
    .out_10(n3_input_and_3_out_10), .out_11(n3_input_and_3_out_11), .out_12(n3_input_and_3_out_12));
  _3_Input_OR_Gate u_3_input_or_2 (
    .in_4(n3_input_and_2_out_10), .in_5(n3_input_and_2_out_10), .in_6(n3_input_and_2_out_11),
    .in_7(n3_input_and_3_out_10), .in_8(n3_input_and_3_out_11), .in_9(n3_input_and_3_out_12), .out_11(C),
    .out_12(B));  // open: in_1, in_2, in_3, out_10
endmodule

module _3_Input_AND_Gate (
  input  in_1,
  input  in_2,
  input  in_3,
  input  in_4,
  input  in_5,
  input  in_6,
  input  in_7,
  input  in_8,
  input  in_9,
  output out_10,
  output out_11,
  output out_12
);

  and and_1 (out_10, in_1, in_2, in_3);
  and and_2 (out_11, in_4, in_5, in_6);
  and and_3 (out_12, in_7, in_8, in_9);
endmodule

module _3_Input_OR_Gate (
  input  in_1,
  input  in_2,
  input  in_3,
  input  in_4,
  input  in_5,
  input  in_6,
  input  in_7,
  input  in_8,
  input  in_9,
  output out_10,
  output out_11,
  output out_12
);

  or or_1 (out_10, in_1, in_2, in_3);
  or or_2 (out_11, in_4, in_5, in_6);
  or or_3 (out_12, in_7, in_8, in_9);
endmodule

module _1_Input_NOT_Gate (
  input  in_1,
  input  in_2,
  input  in_3,
  input  in_4,
  input  in_5,
  input  in_6,
  output out_7,
  output out_8,
  output out_9,
  output out_10,
  output out_11,
  output out_12
);

  not not_1 (out_7, in_1);
  not not_2 (out_8, in_2);
  not not_3 (out_9, in_3);
  not not_4 (out_10, in_4);
  not not_5 (out_11, in_5);
  not not_6 (out_12, in_6);
endmodule
