// Logisim project Assignment-2 Circuit.circ as structural Verilog: 1 circuit, main circuit main
module main (
  input  in_1,
  input  [2:0] INPUT,
  input  ENABLER,
  output SUM,
  output CARRY
);

  Multiplexer #(.select(3)) multiplexer_1 (
    .in0(in_1), .in1(1'b1), .in2(1'b1), .in3(in_1), .in4(1'b1), .in5(in_1), .in6(in_1), .in7(1'b1),
    .out(SUM), .sel(INPUT), .en(ENABLER));
  Multiplexer #(.select(3)) multiplexer_2 (
    .in0(in_1), .in1(in_1), .in2(in_1), .in3(1'b1), .in4(in_1), .in5(1'b1), .in6(1'b1), .in7(1'b1),
    .out(CARRY), .sel(INPUT), .en(ENABLER));
endmodule
