// Logisim project practise work lab 5.circ as structural Verilog: 1 circuit, main circuit main
module main (
  input  in_1,
  input  in_2,
  input  in_3,
  input  in_4,
  input  in_5,
  input  in_6,
  input  A1,
  input  B1,
  input  A2,
  input  B2,
  output [1:0] out_11,
  output out_12,
  output [1:0] out_13,
  output out_14
);

  wire adder_1_cout, adder_3_cout, xor_1_out, xor_2_out;

  Adder #(.width(1)) adder_1 (.a(in_2), .b(in_3), .out(out_11[0]), .cin(in_1), .cout(adder_1_cout));
  Adder #(.width(1)) adder_2 (.a(in_4), .b(in_5), .out(out_11[1]), .cin(adder_1_cout), .cout(out_12));
  Adder #(.width(1)) adder_3 (.a(A1), .b(xor_1_out), .out(out_13[0]), .cin(in_6), .cout(adder_3_cout));
  xor xor_1 (xor_1_out, B1, in_6);
  Adder #(.width(1)) adder_4 (.a(A2), .b(xor_2_out), .out(out_13[1]), .cin(adder_3_cout), .cout(out_14));
  xor xor_2 (xor_2_out, B2, in_6);
endmodule
