// Logisim project Lab Project-1.circ as structural Verilog: 4 circuits, main circuit main
module main (
  input  A,
  input  B,
  input  C,
  input  D,
  output F
);

  wire n1_input_not_1_out_9, n1_input_not_1_out_10, n1_input_not_1_out_11, n1_input_not_1_out_12,
       n4_input_and_1_out_9, n4_input_and_1_out_10, n4_input_and_2_out_9, n4_input_and_2_out_10,
       n4_input_and_3_out_9, n4_input_and_3_out_10, n4_input_and_4_out_9, n4_input_and_4_out_10,
       n4_input_and_5_out_9, n4_input_and_5_out_10, n4_input_and_6_out_9, n4_input_and_6_out_10,
       n4_input_and_7_out_9, n4_input_and_8_out_9, n4_input_and_8_out_10, n4_input_or_1_out_10,
       n4_input_or_2_out_9, n4_input_or_2_out_10, n4_input_or_3_out_9, n4_input_or_3_out_10,
       n4_input_or_4_out_9, n4_input_or_4_out_10;

  _1_Input_NOT_Gate u_1_input_not_1 (
    .in_3(D), .in_4(C), .in_5(B), .in_6(A), .out_9(n1_input_not_1_out_9), .out_10(n1_input_not_1_out_10),
    .out_11(n1_input_not_1_out_11), .out_12(n1_input_not_1_out_12));  // open: in_1, in_2, out_7, out_8
  _4_Input_AND_Gate u_4_input_and_1 (
    .in_1(n1_input_not_1_out_9), .in_2(C), .in_3(n1_input_not_1_out_11), .in_4(A), .in_5(D),
    .in_6(n1_input_not_1_out_10), .in_7(n1_input_not_1_out_11), .in_8(A), .out_9(n4_input_and_1_out_9),
    .out_10(n4_input_and_1_out_10));
  _4_Input_AND_Gate u_4_input_and_2 (
    .in_1(n1_input_not_1_out_9), .in_2(C), .in_3(n1_input_not_1_out_11), .in_4(n1_input_not_1_out_12),
    .in_5(D), .in_6(n1_input_not_1_out_10), .in_7(n1_input_not_1_out_11), .in_8(n1_input_not_1_out_12),
    .out_9(n4_input_and_2_out_9), .out_10(n4_input_and_2_out_10));
  _4_Input_AND_Gate u_4_input_and_3 (
    .in_1(n1_input_not_1_out_9), .in_2(n1_input_not_1_out_10), .in_3(B), .in_4(A), .in_5(D), .in_6(C),
    .in_7(n1_input_not_1_out_11), .in_8(A), .out_9(n4_input_and_3_out_9), .out_10(n4_input_and_3_out_10));
  _4_Input_AND_Gate u_4_input_and_4 (
    .in_1(n1_input_not_1_out_9), .in_2(n1_input_not_1_out_10), .in_3(B), .in_4(n1_input_not_1_out_12),
    .in_5(D), .in_6(C), .in_7(n1_input_not_1_out_11), .in_8(n1_input_not_1_out_12),
    .out_9(n4_input_and_4_out_9), .out_10(n4_input_and_4_out_10));
  _4_Input_AND_Gate u_4_input_and_5 (
    .in_1(n1_input_not_1_out_9), .in_2(C), .in_3(B), .in_4(A), .in_5(D), .in_6(n1_input_not_1_out_10),
    .in_7(B), .in_8(A), .out_9(n4_input_and_5_out_9), .out_10(n4_input_and_5_out_10));
  _4_Input_AND_Gate u_4_input_and_6 (
    .in_1(n1_input_not_1_out_9), .in_2(C), .in_3(B), .in_4(n1_input_not_1_out_12), .in_5(D),
    .in_6(n1_input_not_1_out_10), .in_7(B), .in_8(n1_input_not_1_out_12), .out_9(n4_input_and_6_out_9),
    .out_10(n4_input_and_6_out_10));
  _4_Input_AND_Gate u_4_input_and_7 (
    .in_1(D), .in_2(C), .in_3(B), .in_4(A), .out_9(n4_input_and_7_out_9));  // open: in_5, in_6, in_7, in_8, out_10
  _4_Input_AND_Gate u_4_input_and_8 (
    .in_1(n1_input_not_1_out_9), .in_2(n1_input_not_1_out_10), .in_3(n1_input_not_1_out_11), .in_4(A),
    .in_5(D), .in_6(C), .in_7(B), .in_8(n1_input_not_1_out_12), .out_9(n4_input_and_8_out_9),
    .out_10(n4_input_and_8_out_10));
  or or_1 (F, n4_input_or_4_out_9, n4_input_or_4_out_10);
  _4_Input_OR_Gate u_4_input_or_1 (
    .in_5(D), .in_6(C), .in_7(B), .in_8(A), .out_10(n4_input_or_1_out_10));  // open: in_1, in_2, in_3, in_4, out_9
  _4_Input_OR_Gate u_4_input_or_2 (
    .in_1(n4_input_and_7_out_9), .in_2(n4_input_and_7_out_9), .in_3(n4_input_and_5_out_9),
    .in_4(n4_input_and_5_out_10), .in_5(n4_input_and_3_out_9), .in_6(n4_input_and_3_out_10),
    .in_7(n4_input_and_1_out_9), .in_8(n4_input_and_1_out_10), .out_9(n4_input_or_2_out_9),
    .out_10(n4_input_or_2_out_10));
  _4_Input_OR_Gate u_4_input_or_3 (
    .in_1(n4_input_and_6_out_9), .in_2(n4_input_and_6_out_10), .in_3(n4_input_and_8_out_9),
    .in_4(n4_input_and_8_out_10), .in_5(n4_input_and_4_out_9), .in_6(n4_input_and_4_out_10),
    .in_7(n4_input_and_2_out_9), .in_8(n4_input_and_2_out_10), .out_9(n4_input_or_3_out_9),
    .out_10(n4_input_or_3_out_10));
  _4_Input_OR_Gate u_4_input_or_4 (
    .in_1(n4_input_or_1_out_10), .in_2(n4_input_or_1_out_10), .in_3(n4_input_or_1_out_10),
    .in_4(n4_input_or_1_out_10), .in_5(n4_input_or_3_out_9), .in_6(n4_input_or_3_out_10),
    .in_7(n4_input_or_2_out_9), .in_8(n4_input_or_2_out_10), .out_9(n4_input_or_4_out_9),
    .out_10(n4_input_or_4_out_10));

  // Notes on the sheet:
  //   5
  //   1
  //   6
  //   2
  //   7
  //   3
  //   8
  //   4
endmodule

module _4_Input_AND_Gate (
  input  in_1,
  input  in_2,
  input  in_3,
  input  in_4,
  input  in_5,
  input  in_6,
  input  in_7,
  input  in_8,
  output out_9,
  output out_10
);

  and and_1 (out_9, in_1, in_2, in_3, in_4);
  and and_2 (out_10, in_5, in_6, in_7, in_8);
endmodule

module _4_Input_OR_Gate (
  input  in_1,
  input  in_2,
  input  in_3,
  input  in_4,
  input  in_5,
  input  in_6,
  input  in_7,
  input  in_8,
  output out_9,
  output out_10
);

  or or_1 (out_9, in_1, in_2, in_3, in_4);
  or or_2 (out_10, in_5, in_6, in_7, in_8);
endmodule

module _1_Input_NOT_Gate (
  input  in_1,
  input  in_2,
  input  in_3,
  input  in_4,
  input  in_5,
  input  in_6,
  output out_7,
  output out_8,
  output out_9,
  output out_10,
  output out_11,
  output out_12
);

  not not_1 (out_7, in_1);
  not not_2 (out_8, in_2);
  not not_3 (out_9, in_3);
  not not_4 (out_10, in_4);
  not not_5 (out_11, in_5);
  not not_6 (out_12, in_6);
endmodule
