// Logisim project Lab2 no.2.circ as structural Verilog: 1 circuit, main circuit main
module main (
  input  A,
  input  A_2,
  input  B,
  input  B_2,
  input  A_3,
  input  A_4,
  input  A_5,
  input  B_3,
  input  B_4,
  output out_10,
  output out_11,
  output out_12,
  output out_13,
  output out_14
);

  wire nand_1_out, nand_2_out, nand_3_out, nand_4_out, nand_5_out, nand_6_out, nand_8_out, nand_10_out,
       nand_11_out, nand_12_out;

  nand nand_1 (nand_1_out, A, B_2);
  nand nand_2 (nand_2_out, A_5, B_4);
  nand nand_3 (nand_3_out, A, nand_1_out);
  nand nand_4 (nand_4_out, nand_1_out, B_2);
  nand nand_5 (nand_5_out, A_5, nand_2_out);
  nand nand_6 (nand_6_out, nand_2_out, B_4);
  nand nand_7 (out_11, nand_3_out, nand_4_out);
  nand nand_8 (nand_8_out, nand_5_out, nand_6_out);
  nand nand_9 (out_14, nand_8_out, nand_8_out);
  nand nand_10 (nand_10_out, A_2, B);
  nand nand_11 (nand_11_out, A_4, A_4);
  nand nand_12 (nand_12_out, B_3, B_3);
  nand nand_13 (out_10, nand_10_out, nand_10_out);
  nand nand_14 (out_12, A_3, A_3);
  nand nand_15 (out_13, nand_11_out, nand_12_out);

  // Notes on the sheet:
  //   XOR using NAND Gate
  //   XNOR using NAND Gate
  //   NOT using NAND Gate
  //   AND using NAND Gate
  //   OR using NAND Gate
endmodule
