// Logisim project lab1.circ as structural Verilog: 4 circuits, main circuit main
module main (
  input  A,
  input  B,
  input  C,
  output out_4
);

  wire and_gate_made_by_me_1_out_10, and_gate_made_by_me_1_out_11, and_gate_made_by_me_1_out_12,
       not_gate_made_by_me_1_out_7, not_gate_made_by_me_1_out_8, or_gate_made_by_me_1_out_11;

  NOT_gate_made_by_me not_gate_made_by_me_1 (
    .in_1(A), .in_2(B), .out_7(not_gate_made_by_me_1_out_7), .out_8(not_gate_made_by_me_1_out_8));  // open: in_3, in_4, in_5, in_6, out_9, out_10, out_11, out_12
  AND_gate_made_by_me and_gate_made_by_me_1 (
    .in_3(C), .in_4(B), .in_5(not_gate_made_by_me_1_out_8), .in_6(A), .in_7(C),
    .in_8(not_gate_made_by_me_1_out_7), .out_10(and_gate_made_by_me_1_out_10),
    .out_11(and_gate_made_by_me_1_out_11), .out_12(and_gate_made_by_me_1_out_12));  // open: in_1, in_2, out_9
  OR_gate_made_by_me or_gate_made_by_me_1 (
    .in_5(and_gate_made_by_me_1_out_12), .in_6(and_gate_made_by_me_1_out_11),
    .in_7(or_gate_made_by_me_1_out_11), .in_8(and_gate_made_by_me_1_out_10),
    .out_11(or_gate_made_by_me_1_out_11), .out_12(out_4));  // open: in_1, in_2, in_3, in_4, out_9, out_10
endmodule

module AND_gate_made_by_me (
  input  in_1,
  input  in_2,
  input  in_3,
  input  in_4,
  input  in_5,
  input  in_6,
  input  in_7,
  input  in_8,
  output out_9,
  output out_10,
  output out_11,
  output out_12
);

  and and_1 (out_9, in_1, in_1, in_2);
  and and_2 (out_10, in_3, in_3, in_4);
  and and_3 (out_11, in_5, in_5, in_6);
  and and_4 (out_12, in_7, in_7, in_8);
endmodule

module OR_gate_made_by_me (
  input  in_1,
  input  in_2,
  input  in_3,
  input  in_4,
  input  in_5,
  input  in_6,
  input  in_7,
  input  in_8,
  output out_9,
  output out_10,
  output out_11,
  output out_12
);

  or or_1 (out_9, in_1, in_2);
  or or_2 (out_10, in_3, in_4);
  or or_3 (out_11, in_5, in_6);
  or or_4 (out_12, in_7, in_8);
endmodule

module NOT_gate_made_by_me (
  input  in_1,
  input  in_2,
  input  in_3,
  input  in_4,
  input  in_5,
  input  in_6,
  output out_7,
  output out_8,
  output out_9,
  output out_10,
  output out_11,
  output out_12
);

  not not_1 (out_7, in_1);
  not not_2 (out_8, in_2);
  not not_3 (out_9, in_3);
  not not_4 (out_10, in_4);
  not not_5 (out_11, in_5);
  not not_6 (out_12, in_6);
endmodule
