// Logisim project Lab2 no.3.circ as structural Verilog: 1 circuit, main circuit main
module main (
  input  A,
  input  B,
  input  in_3,
  input  A_2,
  input  B_2,
  input  A_3,
  input  A_4,
  input  B_3,
  input  B_4,
  output out_10,
  output out_11,
  output out_12,
  output out_13,
  output out_14
);

  wire nor_2_out, nor_3_out, nor_4_out, nor_7_out, nor_8_out, nor_9_out, nor_10_out, nor_11_out, nor_12_out,
       nor_13_out;

  nor nor_1 (out_10, in_3, in_3);
  nor nor_2 (nor_2_out, A_2, A_2);
  nor nor_3 (nor_3_out, B_2, B_2);
  nor nor_4 (nor_4_out, A_4, B_3);
  nor nor_5 (out_12, nor_2_out, nor_3_out);
  nor nor_6 (out_13, nor_4_out, nor_4_out);
  nor nor_7 (nor_7_out, A_3, B_4);
  nor nor_8 (nor_8_out, A, A);
  nor nor_9 (nor_9_out, B, B);
  nor nor_10 (nor_10_out, nor_8_out, nor_9_out);
  nor nor_11 (nor_11_out, B, A);
  nor nor_12 (nor_12_out, A_3, nor_7_out);
  nor nor_13 (nor_13_out, nor_7_out, B_4);
  nor nor_14 (out_11, nor_10_out, nor_11_out);
  nor nor_15 (out_14, nor_12_out, nor_13_out);

  // Notes on the sheet:
  //   AND using NOR Gate
  //   NOT using NOR Gate
  //   OR using NOR Gate
  //   XOR using NOR Gate
  //   XNOR using NOR Gate
endmodule
