// Logisim project Lab3 no.1.circ as structural Verilog: 4 circuits, main circuit main
module main (
  input  A,
  input  B,
  input  C,
  output out_4
);

  wire n1_input_not_1_out_8, n1_input_not_1_out_9, n1_input_not_1_out_10, n3_input_and_1_out_10,
       n3_input_and_1_out_11, n3_input_and_1_out_12;

  _1_input_NOT_Gate u_1_input_not_1 (
    .in_2(C), .in_3(B), .in_4(A), .out_8(n1_input_not_1_out_8), .out_9(n1_input_not_1_out_9),
    .out_10(n1_input_not_1_out_10));  // open: in_1, in_5, in_6, out_7, out_11, out_12
  _3_input_AND_Gate u_3_input_and_1 (
    .in_1(n1_input_not_1_out_8), .in_2(B), .in_3(A), .in_4(n1_input_not_1_out_8), .in_5(B),
    .in_6(n1_input_not_1_out_10), .in_7(C), .in_8(n1_input_not_1_out_9), .in_9(n1_input_not_1_out_10),
    .out_10(n3_input_and_1_out_10), .out_11(n3_input_and_1_out_11), .out_12(n3_input_and_1_out_12));
  _3_input_OR_Gate u_3_input_or_1 (
    .in_7(n3_input_and_1_out_10), .in_8(n3_input_and_1_out_11), .in_9(n3_input_and_1_out_12), .out_12(out_4));  // open: in_1, in_2, in_3, in_4, in_5, in_6, out_10, out_11

  // Notes on the sheet:
  //   F=  A'B'C +A'BC'+ABC'
endmodule

module _3_input_OR_Gate (
  input  in_1,
  input  in_2,
  input  in_3,
  input  in_4,
  input  in_5,
  input  in_6,
  input  in_7,
  input  in_8,
  input  in_9,
  output out_10,
  output out_11,
  output out_12
);

  or or_1 (out_10, in_1, in_2, in_3);
  or or_2 (out_11, in_4, in_5, in_6);
  or or_3 (out_12, in_7, in_8, in_9);
endmodule

module _1_input_NOT_Gate (
  input  in_1,
  input  in_2,
  input  in_3,
  input  in_4,
  input  in_5,
  input  in_6,
  output out_7,
  output out_8,
  output out_9,
  output out_10,
  output out_11,
  output out_12
);

  not not_1 (out_7, in_1);
  not not_2 (out_8, in_2);
  not not_3 (out_9, in_3);
  not not_4 (out_10, in_4);
  not not_5 (out_11, in_5);
  not not_6 (out_12, in_6);
endmodule

module _3_input_AND_Gate (
  input  in_1,
  input  in_2,
  input  in_3,
  input  in_4,
  input  in_5,
  input  in_6,
  input  in_7,
  input  in_8,
  input  in_9,
  output out_10,
  output out_11,
  output out_12
);

  and and_1 (out_10, in_1, in_2, in_3);
  and and_2 (out_11, in_4, in_5, in_6);
  and and_3 (out_12, in_7, in_8, in_9);
endmodule
