// Logisim project lab 5 no.1.circ as structural Verilog: 1 circuit, main circuit main
module main (
  input  M,
  input  A1,
  input  B1,
  input  A2,
  input  B2,
  input  A3,
  input  B3,
  input  A4,
  input  B4,
  output [3:0] S4_S3_S2_S1,
  output Co
);

  wire adder_1_cout, adder_2_cout, adder_3_cout, xor_1_out, xor_2_out, xor_3_out, xor_4_out;

  xor xor_1 (xor_1_out, B1, M);
  xor xor_2 (xor_2_out, B2, M);
  xor xor_3 (xor_3_out, B3, M);
  xor xor_4 (xor_4_out, B4, M);
  Adder #(.width(1)) adder_1 (.a(A1), .b(xor_1_out), .out(S4_S3_S2_S1[0]), .cin(M), .cout(adder_1_cout));
  Adder #(.width(1)) adder_2 (.a(A2), .b(xor_2_out), .out(S4_S3_S2_S1[1]), .cin(adder_1_cout), .cout(adder_2_cout));
  Adder #(.width(1)) adder_3 (.a(A3), .b(xor_3_out), .out(S4_S3_S2_S1[2]), .cin(adder_2_cout), .cout(adder_3_cout));
  Adder #(.width(1)) adder_4 (.a(A4), .b(xor_4_out), .out(S4_S3_S2_S1[3]), .cin(adder_3_cout), .cout(Co));
endmodule
