// Logisim project lab 5 no.2.circ as structural Verilog: 2 circuits, main circuit main
module main (
  input  C_in,
  input  C_in_2,
  input  A1,
  input  A2,
  input  A3,
  input  A4,
  input  B1,
  input  B2,
  input  B3,
  input  B4,
  input  in_11,
  output S1,
  output S2,
  output S3,
  output S4,
  output Co__Ignored,
  output C__BCD_Carry
);

  wire AND_2_out, AND_out, n4_bit_adder_circuit_1_co, n4_bit_adder_circuit_1_s1, n4_bit_adder_circuit_1_s2,
       n4_bit_adder_circuit_1_s3, n4_bit_adder_circuit_1_s4, OR_out;

  and AND (AND_out, n4_bit_adder_circuit_1_s3, n4_bit_adder_circuit_1_s4);
  or OR (OR_out, AND_out, AND_2_out);
  or OR_2 (C__BCD_Carry, n4_bit_adder_circuit_1_co, OR_out);
  and AND_2 (AND_2_out, n4_bit_adder_circuit_1_s4, n4_bit_adder_circuit_1_s2);
  _4_Bit_Adder_Circuit u_4_bit_adder_circuit_1 (
    .Ci(C_in_2), .A1(A1), .B1(B1), .A2(A2), .B2(B2), .A3(A3), .B3(B3), .A4(A4), .B4(B4),
    .Co(n4_bit_adder_circuit_1_co), .S1(n4_bit_adder_circuit_1_s1), .S2(n4_bit_adder_circuit_1_s2),
    .S3(n4_bit_adder_circuit_1_s3), .S4(n4_bit_adder_circuit_1_s4));
  _4_Bit_Adder_Circuit u_4_bit_adder_circuit_2 (
    .Ci(C_in), .A1(n4_bit_adder_circuit_1_s1), .B1(in_11), .A2(n4_bit_adder_circuit_1_s2), .B2(C__BCD_Carry),
    .A3(n4_bit_adder_circuit_1_s3), .B3(C__BCD_Carry), .A4(n4_bit_adder_circuit_1_s4), .B4(in_11),
    .Co(Co__Ignored), .S1(S1), .S2(S2), .S3(S3), .S4(S4));
endmodule

module _4_Bit_Adder_Circuit (
  input  Ci,
  input  A1,
  input  B1,
  input  A2,
  input  B2,
  input  A3,
  input  B3,
  input  A4,
  input  B4,
  output S1,
  output S2,
  output S3,
  output S4,
  output Co
);

  wire adder_1_cout, adder_2_cout, adder_3_cout;

  Adder #(.width(1)) adder_1 (.a(A1), .b(B1), .out(S1), .cin(Ci), .cout(adder_1_cout));
  Adder #(.width(1)) adder_2 (.a(A2), .b(B2), .out(S2), .cin(adder_1_cout), .cout(adder_2_cout));
  Adder #(.width(1)) adder_3 (.a(A3), .b(B3), .out(S3), .cin(adder_2_cout), .cout(adder_3_cout));
  Adder #(.width(1)) adder_4 (.a(A4), .b(B4), .out(S4), .cin(adder_3_cout), .cout(Co));
endmodule
