// Logisim project lab6 work-1.circ as structural Verilog: 1 circuit, main circuit main
module main (
  input  _1,
  input  _0,
  input  C,
  input  A__S1,
  input  B__S0,
  input  E,
  output out_7
);

  wire and_1_out, and_2_out, and_3_out, and_4_out, not_1_out, not_2_out, or_1_out, or_2_out;

  not not_1 (not_1_out, A__S1);
  not not_2 (not_2_out, B__S0);
  and and_1 (and_1_out, E, _1, not_1_out, not_2_out);
  and and_2 (and_2_out, E, _0, not_1_out, B__S0);
  and and_3 (and_3_out, E, C, A__S1, not_2_out);
  and and_4 (and_4_out, E, C, A__S1, B__S0);
  or or_1 (or_1_out, and_1_out, and_2_out);
  or or_2 (or_2_out, and_3_out, and_4_out);
  or or_3 (out_7, or_1_out, or_2_out);
endmodule
