// Logisim project lab6 work-2.circ as structural Verilog: 1 circuit, main circuit main
module main (
  input  _0,
  input  D,
  input  [2:0] in_3,
  output out_4
);

  Multiplexer #(.select(3), .enable("false")) multiplexer_1 (
    .in0(1'b1), .in1(D), .in2(D), .in3(_0), .in4(1'b1), .in5(_0), .in6(_0), .in7(1'b1), .out(out_4),
    .sel(in_3));
endmodule
