// Logisim project lab 6 decoder circuit.circ as structural Verilog: 1 circuit, main circuit main
module main (
  input  [2:0] in_1,
  input  G1,
  input  G2A,
  input  G2B,
  output out_5,
  output out_6,
  output out_7,
  output out_8,
  output out_9,
  output out_10,
  output out_11,
  output out_12
);

  wire and_1_out, decoder_1_out0, decoder_1_out1, decoder_1_out2, decoder_1_out3, decoder_1_out4,
       decoder_1_out5, decoder_1_out6, decoder_1_out7, not_1_out, not_2_out;

  not not_1 (not_1_out, G2A);
  not not_2 (not_2_out, G2B);
  and and_1 (and_1_out, G1, not_1_out, not_2_out);
  Decoder #(.select(3)) decoder_1 (
    .out0(decoder_1_out0), .out1(decoder_1_out1), .out2(decoder_1_out2), .out3(decoder_1_out3),
    .out4(decoder_1_out4), .out5(decoder_1_out5), .out6(decoder_1_out6), .out7(decoder_1_out7), .sel(in_1),
    .en(and_1_out));
  not not_3 (out_5, decoder_1_out0);
  not not_4 (out_6, decoder_1_out1);
  not not_5 (out_7, decoder_1_out2);
  not not_6 (out_8, decoder_1_out3);
  not not_7 (out_9, decoder_1_out4);
  not not_8 (out_10, decoder_1_out5);
  not not_9 (out_11, decoder_1_out6);
  not not_10 (out_12, decoder_1_out7);
endmodule
