// Logisim project Counter with JK Flip-flop.circ as structural Verilog: 1 circuit, main circuit main
module main (
  input  in_1
);

  wire and_1_out, and_2_out, and_3_out, and_4_out, clock_1_out, j_k_ff_1_q, j_k_ff_1_qn, j_k_ff_2_q,
       j_k_ff_2_qn, not_1_out, or_1_out, or_2_out;

  not not_1 (not_1_out, in_1);
  and and_1 (and_1_out, not_1_out, j_k_ff_1_qn, j_k_ff_2_q);
  and and_2 (and_2_out, in_1, j_k_ff_1_qn, j_k_ff_2_qn);
  and and_3 (and_3_out, not_1_out, j_k_ff_1_q, j_k_ff_2_q);
  and and_4 (and_4_out, in_1, j_k_ff_1_q, j_k_ff_2_qn);
  or or_1 (or_1_out, and_1_out, and_2_out);
  or or_2 (or_2_out, and_3_out, and_4_out);
  Clock clock_1 (.out(clock_1_out));
  J_K_Flip_Flop j_k_ff_1 (
    .J(or_1_out), .clk(clock_1_out), .K(or_2_out), .Q(j_k_ff_1_q), .Qn(j_k_ff_1_qn));  // open: preset, en, reset
  J_K_Flip_Flop j_k_ff_2 (
    .J(j_k_ff_2_qn), .clk(clock_1_out), .K(j_k_ff_2_q), .Q(j_k_ff_2_q), .Qn(j_k_ff_2_qn));  // open: preset, en, reset
endmodule
