// Logisim project Counter with T Flip-flop.circ as structural Verilog: 1 circuit, main circuit main
module main (
  input  in_1
);

  wire and_1_out, and_2_out, clock_1_out, not_1_out, or_1_out, t_ff_1_q, t_ff_2_q, t_ff_2_qn;

  not not_1 (not_1_out, in_1);
  and and_1 (and_1_out, not_1_out, t_ff_2_q);
  and and_2 (and_2_out, in_1, t_ff_2_qn);
  or or_1 (or_1_out, and_1_out, and_2_out);
  Clock clock_1 (.out(clock_1_out));
  T_Flip_Flop t_ff_1 (.clk(clock_1_out), .T(or_1_out), .Q(t_ff_1_q));  // open: Qn, preset, reset, en
  T_Flip_Flop t_ff_2 (.clk(clock_1_out), .T(1'b1), .Q(t_ff_2_q), .Qn(t_ff_2_qn));  // open: preset, reset, en
endmodule
